# Fritzing sketch sketch (saved by Fritzing 0.9.2b)
circuit board: 7.70632cm x 6.21336cm

parts:
  INA219 = INA219 High Side DC Current Sensor Breakout [part_number=904]
  Arduino_Nano_v3_0 = Arduino Nano (Rev3.0)
  Part1 = OLED Monochrome 128x64 1.3 inch [part_number=938]

nets:
  VCC: INA219.VCC, Arduino_Nano_v3_0.VIN
  GND: INA219.GND, Arduino_Nano_v3_0.GND, Part1.GND
  N1: INA219.SCL, Arduino_Nano_v3_0.A5, Part1.SCL
  N2: INA219.SDA, Arduino_Nano_v3_0.A4, Part1.SDA
  3V3: Arduino_Nano_v3_0.3V3, Part1.VCC

custom parts:
  INA219 High Side DC Current Sensor Breakout: This breakout board will solve all your power-monitoring problems. Instead of struggling with two multimeters, you can just use the handy INA219B chip on this breakout to both measure both the high side voltage and DC current draw over I2C with 1% precision. Most current-measuring devices such as our current panel meter are only good for low side measuring. That means that unless you want to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
  OLED Monochrome 128x64 1.3 inch: These displays are small, only about 1.3" diagonal, but very readable due to the high contrast of an OLED display. This display is made of 128x64 individual white OLED pixels, each one is turned on or off by the controller chip. Because the display makes its own light, no backlight is required. This reduces the power required to run the OLED and is why the display has such high contrast; we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
